# Fritzing sketch 5050-led-strip (saved by Fritzing 0.9.3b)
breadboards: 1

parts:
  U1 = ESP32-38PinWide [part_number=ESP32-38PinWide]
  Q1 = NPN-Transistor [package="TO92 [THT]"]
  Q2 = NPN-Transistor [package="TO92 [THT]"]
  Q3 = NPN-Transistor [package="TO92 [THT]"]
  R1 = Resistor [tolerance=±5% resistance=1k package="0402 [SMD]"]
  R2 = Resistor [tolerance=±5% resistance=1k package="0402 [SMD]"]
  R3 = Resistor [tolerance=±5% resistance=1k package="0402 [SMD]"]

nets:
  N1: U1.GPIO27, R3.Pin_0
  N2: U1.GPIO14, R2.Pin_0
  N3: U1.GPIO12, R1.Pin_0
  N4: U1.GND, Q1.C, Q2.C, Q3.C
  N5: Q1.B, R3.Pin_1
  N6: Q2.B, R1.Pin_1
  N7: Q3.B, R2.Pin_1

custom parts:
  ESP32-38PinWide: Generic 38-Pin ESP32 with wide format (only access to one side of pins on a breadboard) based on Stephen Lilley's HiLetgo ESP-WROOM-32 ESP32 ESP-32S Development Board.
