# Fritzing sketch BME280-tutorial (saved by Fritzing 0.9.3b)
breadboards: 1

parts:
  WeMos_D1_Mini1 = WeMos D1 Mini
  Part1 = BME280 Breakout

nets:
  3V3: WeMos_D1_Mini1.3V3, Part1.3.3V
  N1: WeMos_D1_Mini1.D1, Part1.SCK/SCL
  N2: WeMos_D1_Mini1.D2, Part1.SDI/SDA
  N3: WeMos_D1_Mini1.G, Part1.GND
