# Fritzing sketch BMP180-tutorial (saved by Fritzing 0.9.3b)
breadboards: 1

parts:
  WeMos_D1_Mini1 = WeMos D1 Mini
  Bauteil4 = Barometric Pressure Sensor - BMP085 Breakout

nets:
  5V: WeMos_D1_Mini1.5V, Bauteil4.VCC
  N1: WeMos_D1_Mini1.D1, Bauteil4.SCL
  N2: WeMos_D1_Mini1.D2, Bauteil4.SDA
  N3: WeMos_D1_Mini1.G, Bauteil4.GND
