# Fritzing sketch Capacitive-Soil-Moisture-Sensor (saved by Fritzing 0.9.3b)

parts:
  Capacitive_Soil_Moisture_Sensor1 = DFRobot Capacitive Soil Moisture Sensor V1.0 [part_number=SEN0193]
  NodeMCU_v1 = NodeMCU v3 LoLin [part_number=ESP8266]

nets:
  N1: Capacitive_Soil_Moisture_Sensor1.A, NodeMCU_v1.A0
  VCC: Capacitive_Soil_Moisture_Sensor1.VCC, NodeMCU_v1.VIN
  GND: Capacitive_Soil_Moisture_Sensor1.GND, NodeMCU_v1.GND

custom parts:
  DFRobot Capacitive Soil Moisture Sensor V1.0: DFRobot Capacitive Soil Moisture Sensor V1.0 This product measures soil moisture levels by capacitive sensing, rather than resistive sensing like other types of moisture sensor. It is made of a corrosion resistant material giving it a long service life. Insert it into soil and impress your friends with the real-time soil moisture data! The product includes an on-board voltage regulator which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
  NodeMCU v3 LoLin: NodeMCU v3 LoLin NodeMCU (http://www.nodemcu.com/) is an open source IoT platform. It includes firmware (https://nodemcu-build.com/) which runs on the ESP8266 Wi-Fi SoC from Espressif Systems, and hardware which is based on the ESP-12E module. The term "NodeMCU" by default refers to the firmware rather than the dev kits. The firmware uses the Lua scripting language. It is based on the eLua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
