# Fritzing sketch LM335-tutorial (saved by Fritzing 0.9.3b)
breadboards: 1

parts:
  WeMos_D1_Mini1 = WeMos D1 Mini
  T1 = LM35 Temperature Sensor [package="TO92 [THT]"]
  R1 = Resistor [tolerance=±5% resistance=2.2k package="0805 [SMD]"]

nets:
  N1: WeMos_D1_Mini1.5V, R1.Pin_1
  N2: WeMos_D1_Mini1.A0, T1.Vout, R1.Pin_0
  N3: WeMos_D1_Mini1.G, T1.+Vs, T1.GND
