# Fritzing sketch LM35-tutorial (saved by Fritzing 0.9.3b)
breadboards: 1

parts:
  WeMos_D1_Mini1 = WeMos D1 Mini
  T1 = LM35 Temperature Sensor [package="TO92 [THT]"]

nets:
  N1: WeMos_D1_Mini1.A0, T1.Vout
  N2: WeMos_D1_Mini1.G, T1.+Vs, T1.GND
