# Fritzing sketch Ultrasonic-Sensor (saved by Fritzing 0.9.3b)

parts:
  NodeMCU_v1 = NodeMCU v3 LoLin [part_number=ESP8266]
  Part1 = SRF05 Ultrasonic Rangefinder

nets:
  GND: NodeMCU_v1.GND, Part1.GND
  N1: NodeMCU_v1.D5, Part1.Echo
  N2: NodeMCU_v1.D6, Part1.Trig
  VIN: NodeMCU_v1.VIN, Part1.VCC

custom parts:
  NodeMCU v3 LoLin: NodeMCU v3 LoLin NodeMCU (http://www.nodemcu.com/) is an open source IoT platform. It includes firmware (https://nodemcu-build.com/) which runs on the ESP8266 Wi-Fi SoC from Espressif Systems, and hardware which is based on the ESP-12E module. The term "NodeMCU" by default refers to the firmware rather than the dev kits. The firmware uses the Lua scripting language. It is based on the eLua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
