# Fritzing sketch contact-sensor (saved by Fritzing 0.9.3b)
breadboards: 1

parts:
  S1 = Reed switch [package=THT]
  WeMos_D1_Mini1 = WeMos D1 Mini

nets:
  N1: S1.pin_1, WeMos_D1_Mini1.D2
  N2: S1.pin_2, WeMos_D1_Mini1.G
