# Fritzing sketch motion-sensor (saved by Fritzing 0.9.3b)
breadboards: 1

parts:
  WeMos_D1_Mini1 = WeMos D1 Mini
  PIR = HC-SR501 Body Sensor Module

nets:
  5V: WeMos_D1_Mini1.5V, PIR.VCC
  N1: WeMos_D1_Mini1.D1, PIR.OUT
  N2: WeMos_D1_Mini1.G, PIR.GND

custom parts:
  HC-SR501 Body Sensor Module: Pyroelectric Infrared PIR Motion Sensor Detector Module
