# Fritzing sketch switch-tutorial (saved by Fritzing 0.9.3b)
breadboards: 1

parts:
  WeMos_D1_Mini1 = WeMos D1 Mini
  WeMos_D1_Mini_Relay_Shield_V1 = WeMos D1 Mini Relay Shield V2
  WeMos_D1_Mini_Relay_Shield1 = WeMos D1 Mini Relay Shield  # not connected

nets (from the breadboard view):
  5V: WeMos_D1_Mini1.5V, WeMos_D1_Mini_Relay_Shield_V1.5V
  N1: WeMos_D1_Mini1.D6, WeMos_D1_Mini_Relay_Shield_V1.D5
  N2: WeMos_D1_Mini1.G, WeMos_D1_Mini_Relay_Shield_V1.G
