# Fritzing sketch water_sensor (saved by Fritzing 0.9.3b)

parts:
  Water_Level_Sensor1 = Water Level Sensor
  NodeMCU_v1 = NodeMCU v3 LoLin [part_number=ESP8266]

nets:
  N1: Water_Level_Sensor1.SIG, NodeMCU_v1.A0
  N2: Water_Level_Sensor1.VCC, NodeMCU_v1.D2
  GND: Water_Level_Sensor1.GND, NodeMCU_v1.GND

custom parts:
  Water Level Sensor: A water level sensor. This sensor operates at 3V to 5V. The Sig (signal) pin outputs an analogue signal that is in proportion to the amount of water in contact with the sensor.
  NodeMCU v3 LoLin: NodeMCU v3 LoLin NodeMCU (http://www.nodemcu.com/) is an open source IoT platform. It includes firmware (https://nodemcu-build.com/) which runs on the ESP8266 Wi-Fi SoC from Espressif Systems, and hardware which is based on the ESP-12E module. The term "NodeMCU" by default refers to the firmware rather than the dev kits. The firmware uses the Lua scripting language. It is based on the eLua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
